// Logisim project ALU with registers.circ as structural Verilog: 11 circuits, main circuit 1bitfulladder
module _1bitfulladder (
  input  Cin,
  input  Ai,
  input  Bi,
  output Si,
  output Cout
);

  wire and_1_out, and_2_out, and_3_out, and_4_out, and_5_out, and_6_out, and_7_out, not_1_out, not_2_out,
       not_3_out, not_4_out, not_5_out, not_6_out;

  not not_1 (not_1_out, Cin);
  not not_2 (not_2_out, Ai);
  not not_3 (not_3_out, Cin);
  not not_4 (not_4_out, Bi);
  not not_5 (not_5_out, Ai);
  not not_6 (not_6_out, Bi);
  and and_1 (and_1_out, Ai, Bi);
  and and_2 (and_2_out, Cin, Bi);
  and and_3 (and_3_out, Cin, Ai);
  and and_4 (and_4_out, not_1_out, not_2_out, Bi);
  and and_5 (and_5_out, not_3_out, Ai, not_4_out);
  and and_6 (and_6_out, Cin, not_5_out, not_6_out);
  and and_7 (and_7_out, Cin, Ai, Bi);
  or or_1 (Cout, and_1_out, and_2_out, and_3_out);
  or or_2 (Si, and_4_out, and_5_out, and_6_out, and_7_out);
endmodule

module _4bitadder (
  input  B3,
  input  B2,
  input  B1,
  input  B0,
  input  A3,
  input  A2,
  input  A1,
  input  A0,
  input  Cin,
  output S3,
  output S2,
  output S1,
  output S0,
  output Overflow
);

  wire n1bitfulladder_1_cout, n1bitfulladder_2_cout, n1bitfulladder_3_cout, n1bitfulladder_4_cout;

  _1bitfulladder u_1bitfulladder_1 (
    .Cin(n1bitfulladder_2_cout), .Ai(A3), .Bi(B3), .Si(S3), .Cout(n1bitfulladder_1_cout));
  xor xor_1 (Overflow, n1bitfulladder_2_cout, n1bitfulladder_1_cout);
  _1bitfulladder u_1bitfulladder_2 (
    .Cin(n1bitfulladder_3_cout), .Ai(A2), .Bi(B2), .Si(S2), .Cout(n1bitfulladder_2_cout));
  _1bitfulladder u_1bitfulladder_3 (
    .Cin(n1bitfulladder_4_cout), .Ai(A1), .Bi(B1), .Si(S1), .Cout(n1bitfulladder_3_cout));
  _1bitfulladder u_1bitfulladder_4 (.Cin(Cin), .Ai(A0), .Bi(B0), .Si(S0), .Cout(n1bitfulladder_4_cout));
endmodule

module _4bitsubtractor (
  input  B3,
  input  B2,
  input  B1,
  input  B0,
  input  A3,
  input  A2,
  input  A1,
  input  A0,
  output C0,
  output Cout,
  output S3,
  output S2,
  output S1,
  output S0,
  output Overflow
);

  wire n1bitfulladder_2_cout, n1bitfulladder_3_cout, n1bitfulladder_4_cout, not_1_out, not_2_out, not_3_out,
       not_4_out;

  not not_1 (not_1_out, B3);
  _1bitfulladder u_1bitfulladder_1 (.Cin(n1bitfulladder_2_cout), .Ai(A3), .Bi(not_1_out), .Si(S3), .Cout(Cout));
  xor xor_1 (Overflow, n1bitfulladder_2_cout, Cout);
  not not_2 (not_2_out, B2);
  _1bitfulladder u_1bitfulladder_2 (
    .Cin(n1bitfulladder_3_cout), .Ai(A2), .Bi(not_2_out), .Si(S2), .Cout(n1bitfulladder_2_cout));
  not not_3 (not_3_out, B1);
  _1bitfulladder u_1bitfulladder_3 (
    .Cin(n1bitfulladder_4_cout), .Ai(A1), .Bi(not_3_out), .Si(S1), .Cout(n1bitfulladder_3_cout));
  not not_4 (not_4_out, B0);
  _1bitfulladder u_1bitfulladder_4 (.Cin(1'b1), .Ai(A0), .Bi(not_4_out), .Si(S0), .Cout(n1bitfulladder_4_cout));

  assign C0 = 1'b1;
endmodule

module _4bitaddersubtractor (
  input  Mode,
  input  Enable,
  input  B3,
  input  B2,
  input  B1,
  input  B0,
  input  A3,
  input  A2,
  input  A1,
  input  A0,
  output S3,
  output S2,
  output S1,
  output S0,
  output Overflow,
  output Carryout
);

  wire and_1_out, and_2_out, and_3_out, and_4_out, and_5_out, and_6_out, controlled_buffer_1_out,
       controlled_buffer_2_out, controlled_buffer_3_out, controlled_buffer_4_out, controlled_buffer_5_out,
       controlled_buffer_6_out, controlled_buffer_7_out, controlled_buffer_8_out, n1bitfulladder_1_cout,
       n1bitfulladder_1_si, n1bitfulladder_2_cout, n1bitfulladder_2_si, n1bitfulladder_3_cout,
       n1bitfulladder_3_si, n1bitfulladder_4_cout, n1bitfulladder_4_si, xor_1_out, xor_2_out, xor_3_out,
       xor_4_out, xor_5_out;

  xor xor_1 (xor_1_out, Mode, B3);
  assign controlled_buffer_1_out = Enable ? A3 : 1'bz;  // Controlled_Buffer controlled_buffer_1
  assign controlled_buffer_2_out = Enable ? xor_1_out : 1'bz;  // Controlled_Buffer controlled_buffer_2
  _1bitfulladder u_1bitfulladder_1 (
    .Cin(n1bitfulladder_2_cout), .Ai(controlled_buffer_1_out), .Bi(controlled_buffer_2_out),
    .Si(n1bitfulladder_1_si), .Cout(n1bitfulladder_1_cout));
  xor xor_2 (xor_2_out, n1bitfulladder_2_cout, n1bitfulladder_1_cout);
  xor xor_3 (xor_3_out, Mode, B2);
  assign controlled_buffer_3_out = Mode ? A2 : 1'bz;  // Controlled_Buffer controlled_buffer_3
  assign controlled_buffer_4_out = Mode ? xor_3_out : 1'bz;  // Controlled_Buffer controlled_buffer_4
  _1bitfulladder u_1bitfulladder_2 (
    .Cin(n1bitfulladder_3_cout), .Ai(controlled_buffer_3_out), .Bi(controlled_buffer_4_out),
    .Si(n1bitfulladder_2_si), .Cout(n1bitfulladder_2_cout));
  xor xor_4 (xor_4_out, Mode, B1);
  assign controlled_buffer_5_out = Mode ? A1 : 1'bz;  // Controlled_Buffer controlled_buffer_5
  assign controlled_buffer_6_out = Mode ? xor_4_out : 1'bz;  // Controlled_Buffer controlled_buffer_6
  assign controlled_buffer_7_out = Mode ? A0 : 1'bz;  // Controlled_Buffer controlled_buffer_7
  _1bitfulladder u_1bitfulladder_3 (
    .Cin(n1bitfulladder_4_cout), .Ai(controlled_buffer_5_out), .Bi(controlled_buffer_6_out),
    .Si(n1bitfulladder_3_si), .Cout(n1bitfulladder_3_cout));
  xor xor_5 (xor_5_out, Mode, B0);
  assign controlled_buffer_8_out = Mode ? xor_5_out : 1'bz;  // Controlled_Buffer controlled_buffer_8
  _1bitfulladder u_1bitfulladder_4 (
    .Cin(Mode), .Ai(controlled_buffer_7_out), .Bi(controlled_buffer_8_out), .Si(n1bitfulladder_4_si),
    .Cout(n1bitfulladder_4_cout));
  and and_1 (and_1_out, Enable, n1bitfulladder_1_si);
  and and_2 (and_2_out, Enable, n1bitfulladder_2_si);
  and and_3 (and_3_out, Enable, n1bitfulladder_3_si);
  and and_4 (and_4_out, Enable, n1bitfulladder_4_si);
  and and_5 (and_5_out, Enable, xor_2_out);
  and and_6 (and_6_out, Enable, n1bitfulladder_1_cout);
  assign S3 = Enable ? and_1_out : 1'bz;  // Controlled_Buffer controlled_buffer_9
  assign S2 = Enable ? and_2_out : 1'bz;  // Controlled_Buffer controlled_buffer_10
  assign S1 = Enable ? and_3_out : 1'bz;  // Controlled_Buffer controlled_buffer_11
  assign S0 = Enable ? and_4_out : 1'bz;  // Controlled_Buffer controlled_buffer_12
  assign Overflow = Enable ? and_5_out : 1'bz;  // Controlled_Buffer controlled_buffer_13
  assign Carryout = Enable ? and_6_out : 1'bz;  // Controlled_Buffer controlled_buffer_14
endmodule

module _1_1ALU (
  input  A3,
  input  A2,
  input  A1,
  input  A0,
  input  B3,
  input  B2,
  input  B1,
  input  B0,
  input  L,
  input  S1,
  input  S0,
  input  Co,
  input  in_13,
  input  in_14,
  input  in_15,
  input  in_16,
  input  in_17,
  input  in_18,
  output [3:0] A,
  output [3:0] B,
  output [3:0] AandB,
  output [3:0] AorB,
  output AandB_2,
  output [3:0] AxorB,
  output AorB_2,
  output [3:0] AnxorB,
  output AxorB_2,
  output AnxorB_2,
  output AgreaterthanB,
  output AequalsB,
  output AlessthanB,
  output Aplus1,
  output S3,
  output S2,
  output S1_2,
  output S0_2,
  output AplusB,
  output Overflow,
  output AplusBplus1,
  output N__Negative_Sign,
  output AminusB,
  output S3_2,
  output S__Sign,
  output S2_2,
  output S1_3,
  output S0_3,
  output Overflow_2,
  output BminusA,
  output S3_3,
  output S2_3,
  output S1_4,
  output S0_4,
  output Overflow_3,
  output V__Overflow,
  output C__Carryout,
  output S3_4,
  output S2_4,
  output Z__Zero,
  output S1_5,
  output S0_5,
  output Overflow_4,
  output S3_5,
  output S2_5,
  output S1_6,
  output S0_6,
  output Overflow_5
);

  wire and_13_out, comparison_1_a___b, comparison_1_a___b_2, comparison_1_a___b_3,
       n4bitaddersubtractor_3_carryout, n4bitaddersubtractor_3_overflow, n4bitaddersubtractor_3_s0,
       n4bitaddersubtractor_3_s1, n4bitaddersubtractor_3_s2, n4bitaddersubtractor_3_s3,
       n4bitaddersubtractor_6_carryout, n4bitaddersubtractor_6_overflow, n7segmentdisplay_1_sa,
       n7segmentdisplay_1_sb, n7segmentdisplay_1_sc, n7segmentdisplay_1_sd, n7segmentdisplay_1_se,
       n7segmentdisplay_1_sf, n7segmentdisplay_1_sg, not_1_out, not_2_out, not_3_out, not_4_out, not_5_out,
       not_6_out, not_7_out, not_8_out, not_9_out, not_10_out, not_11_out, not_12_out, not_13_out,
       not_14_out, not_15_out, not_16_out, not_17_out, not_18_out, not_19_out, not_20_out, or_1_out, or_2_out;

  not not_1 (not_1_out, L);
  not not_2 (not_2_out, S1);
  not not_3 (not_3_out, S0);
  not not_4 (not_4_out, L);
  not not_5 (not_5_out, S1);
  not not_6 (not_6_out, L);
  not not_7 (not_7_out, S0);
  not not_8 (not_8_out, L);
  not not_9 (not_9_out, S1);
  not not_10 (not_10_out, S0);
  not not_11 (not_11_out, Co);
  not not_12 (not_12_out, S1);
  not not_13 (not_13_out, S0);
  not not_14 (not_14_out, S1);
  not not_15 (not_15_out, Co);
  not not_16 (not_16_out, S1);
  not not_17 (not_17_out, S0);
  not not_18 (not_18_out, Co);
  not not_19 (not_19_out, S0);
  not not_20 (not_20_out, Co);
  and and_1 (BminusA, L, S1, S0, Co);
  and and_2 (AandB_2, not_1_out, not_2_out, not_3_out);
  and and_3 (AorB_2, not_4_out, not_5_out, S0);
  and and_4 (AxorB_2, not_6_out, S1, not_7_out);
  and and_5 (AnxorB_2, not_8_out, S1, S0);
  and and_6 (AgreaterthanB, L, not_9_out, not_10_out, not_11_out);
  and and_7 (AequalsB, L, not_12_out, not_13_out, Co);
  and and_8 (AlessthanB, L, not_14_out, S0, not_15_out);
  and and_9 (Aplus1, L, not_16_out, S0, Co);
  and and_10 (AplusB, L, S1, not_17_out, not_18_out);
  and and_11 (AplusBplus1, L, S1, not_19_out, Co);
  and and_12 (AminusB, L, S1, S0, not_20_out);
  _4bitaddersubtractor u_4bitaddersubtractor_1 (
    .Mode(in_13), .B3(in_14), .B2(in_14), .B1(in_14), .B0(Aplus1), .A3(A3), .A2(A2), .A1(A1), .A0(A0),
    .S3(S3), .S2(S2), .S1(S1_2), .S0(S0_2), .Overflow(Overflow), .Enable(Aplus1), .Carryout(C__Carryout));
  _4bitaddersubtractor u_4bitaddersubtractor_2 (
    .Mode(in_15), .B3(B3), .B2(B2), .B1(B1), .B0(B0), .A3(A3), .A2(A2), .A1(A1), .A0(A0), .S3(S3), .S2(S2),
    .S1(S1_2), .S0(S0_2), .Overflow(Overflow), .Enable(AplusB), .Carryout(C__Carryout));
  _4bitaddersubtractor u_4bitaddersubtractor_3 (
    .Mode(in_18), .B3(B3), .B2(B2), .B1(B1), .B0(B0), .A3(A3), .A2(A2), .A1(A1), .A0(A0),
    .S3(n4bitaddersubtractor_3_s3), .S2(n4bitaddersubtractor_3_s2), .S1(n4bitaddersubtractor_3_s1),
    .S0(n4bitaddersubtractor_3_s0), .Overflow(n4bitaddersubtractor_3_overflow), .Enable(AplusBplus1),
    .Carryout(n4bitaddersubtractor_3_carryout));
  _4bitaddersubtractor u_4bitaddersubtractor_4 (
    .Mode(AminusB), .B3(B3), .B2(B2), .B1(B1), .B0(B0), .A3(A3), .A2(A2), .A1(A1), .A0(A0), .S3(S3), .S2(S2),
    .S1(S1_2), .S0(S0_2), .Overflow(Overflow), .Enable(AminusB), .Carryout(C__Carryout));
  _4bitaddersubtractor u_4bitaddersubtractor_5 (
    .Mode(BminusA), .B3(A3), .B2(A2), .B1(A1), .B0(A0), .A3(B3), .A2(B2), .A1(B1), .A0(B0), .S3(S3), .S2(S2),
    .S1(S1_2), .S0(S0_2), .Overflow(Overflow), .Enable(BminusA), .Carryout(C__Carryout));
  _4bitaddersubtractor u_4bitaddersubtractor_6 (
    .Mode(in_16), .B3(in_17), .B2(in_17), .B1(in_17), .B0(AplusBplus1), .A3(n4bitaddersubtractor_3_s3),
    .A2(n4bitaddersubtractor_3_s2), .A1(n4bitaddersubtractor_3_s1), .A0(n4bitaddersubtractor_3_s0), .S3(S3),
    .S2(S2), .S1(S1_2), .S0(S0_2), .Overflow(n4bitaddersubtractor_6_overflow), .Enable(AplusBplus1),
    .Carryout(n4bitaddersubtractor_6_carryout));
  or or_1 (or_1_out, n4bitaddersubtractor_6_overflow, n4bitaddersubtractor_3_overflow);
  assign Overflow = AplusBplus1 ? or_1_out : 1'bz;  // Controlled_Buffer controlled_buffer_1
  assign C__Carryout = AplusBplus1 ? or_2_out : 1'bz;  // Controlled_Buffer controlled_buffer_2
  or or_2 (or_2_out, n4bitaddersubtractor_6_carryout, n4bitaddersubtractor_3_carryout);
  LogicOperations logicoperations_1 (
    .in_1({A3, A2, A1, A0}), .in_2({B3, B2, B1, B0}), .AandB(AandB_2), .AorB(AorB_2), .AxorB(AxorB_2),
    .AnxorB(AnxorB_2), .AandB_2(AandB), .AorB_2(AorB), .AxorB_2(AxorB), .AnxorB_2(AnxorB));
  _7segmentdisplay u_7segmentdisplay_1 (
    .D3(S3), .D2(S2), .Sa(n7segmentdisplay_1_sa), .D1(S1_2), .D0(S0_2), .Sb(n7segmentdisplay_1_sb),
    .Sc(n7segmentdisplay_1_sc), .Sd(n7segmentdisplay_1_sd), .Se(n7segmentdisplay_1_se),
    .Sf(n7segmentdisplay_1_sf), .Sg(n7segmentdisplay_1_sg), .AlargerthanB(comparison_1_a___b_2),
    .AequalsB(comparison_1_a___b), .AlessthanB(comparison_1_a___b_3));
  Comparison comparison_1 (
    .A___B(comparison_1_a___b), .A___B_2(comparison_1_a___b_2), .A___B_3(comparison_1_a___b_3),
    .AgreaterthanB(AgreaterthanB), .AequalsB(AequalsB), .AlessthanB(AlessthanB), .A({A3, A2, A1, A0}),
    .B({B3, B2, B1, B0}));
  and and_13 (and_13_out, S2, S1_2, S0_2);
  not not_21 (Z__Zero, and_13_out);
  _7_Segment_Display u_7_segment_display_1 (
    .g(n7segmentdisplay_1_sg), .f(n7segmentdisplay_1_sf), .a(n7segmentdisplay_1_sa),
    .b(n7segmentdisplay_1_sb), .e(n7segmentdisplay_1_se), .d(n7segmentdisplay_1_sd), .c(n7segmentdisplay_1_sc));  // open: dp

  assign A = {A3, A2, A1, A0};
  assign B = {B3, B2, B1, B0};
  assign Overflow_2 = Overflow;
  assign Overflow_3 = Overflow;
  assign Overflow_4 = Overflow;
  assign Overflow_5 = Overflow;
  assign S0_3 = S0_2;
  assign S0_4 = S0_2;
  assign S0_5 = S0_2;
  assign S0_6 = S0_2;
  assign S1_3 = S1_2;
  assign S1_4 = S1_2;
  assign S1_5 = S1_2;
  assign S1_6 = S1_2;
  assign S2_2 = S2;
  assign S2_3 = S2;
  assign S2_4 = S2;
  assign S2_5 = S2;
  assign S3_2 = S3;
  assign S3_3 = S3;
  assign S3_4 = S3;
  assign S3_5 = S3;
  assign S__Sign = N__Negative_Sign;
  assign V__Overflow = Overflow;
endmodule

module LogicOperations (
  input  [3:0] in_1,
  input  [3:0] in_2,
  input  AandB,
  input  AorB,
  input  AxorB,
  input  AnxorB,
  output [3:0] AandB_2,
  output [3:0] AorB_2,
  output [3:0] AxorB_2,
  output [3:0] AnxorB_2
);

  wire [3:0] and_1_out, or_1_out, xnor_1_out, xor_1_out;

  assign and_1_out = in_1 & in_2;  // AND_Gate and_1, 4 bits wide
  assign or_1_out = in_1 | in_2;  // OR_Gate or_1, 4 bits wide
  assign xor_1_out = in_1 ^ in_2;  // XOR_Gate xor_1, 4 bits wide
  assign xnor_1_out = ~(in_1 ^ in_2);  // XNOR_Gate xnor_1, 4 bits wide
  assign AandB_2 = AandB ? and_1_out : 4'bz;  // Controlled_Buffer controlled_buffer_1
  assign AorB_2 = AorB ? or_1_out : 4'bz;  // Controlled_Buffer controlled_buffer_2
  assign AxorB_2 = AxorB ? xor_1_out : 4'bz;  // Controlled_Buffer controlled_buffer_3
  assign AnxorB_2 = AnxorB ? xnor_1_out : 4'bz;  // Controlled_Buffer controlled_buffer_4
endmodule

module GreaterOrEqualsOrLess (
  input  A3,
  input  A2,
  input  A1,
  input  A0,
  input  B3,
  input  B2,
  input  B1,
  input  B0,
  input  AgreaterthanB,
  input  AequalsB,
  input  AlessthanB,
  output AgreaterthanB_2,
  output AequalsB_2,
  output AlessthanB_2
);

  wire and_1_out, and_2_out, and_3_out, and_4_out, and_6_out, and_7_out, and_8_out, and_9_out, not_1_out,
       not_2_out, not_3_out, not_4_out, not_5_out, not_6_out, not_7_out, not_8_out, or_1_out, or_2_out,
       xnor_1_out, xnor_2_out, xnor_3_out, xnor_4_out, xnor_5_out, xnor_6_out, xnor_7_out, xnor_8_out,
       xnor_9_out, xnor_10_out, xnor_11_out, xnor_12_out, xnor_13_out, xnor_14_out, xnor_15_out, xnor_16_out;

  not not_1 (not_1_out, B3);
  xnor xnor_1 (xnor_1_out, A3, B3);
  not not_2 (not_2_out, B2);
  xnor xnor_2 (xnor_2_out, A3, B3);
  xnor xnor_3 (xnor_3_out, A2, B2);
  not not_3 (not_3_out, B1);
  xnor xnor_4 (xnor_4_out, A3, B3);
  xnor xnor_5 (xnor_5_out, A2, B2);
  xnor xnor_6 (xnor_6_out, A1, B1);
  not not_4 (not_4_out, B0);
  xnor xnor_7 (xnor_7_out, A3, B3);
  xnor xnor_8 (xnor_8_out, A2, B2);
  xnor xnor_9 (xnor_9_out, A1, B1);
  xnor xnor_10 (xnor_10_out, A0, B0);
  not not_5 (not_5_out, A3);
  xnor xnor_11 (xnor_11_out, B3, A3);
  not not_6 (not_6_out, A2);
  xnor xnor_12 (xnor_12_out, B3, A3);
  xnor xnor_13 (xnor_13_out, B2, A2);
  not not_7 (not_7_out, A1);
  xnor xnor_14 (xnor_14_out, B3, A3);
  xnor xnor_15 (xnor_15_out, B2, A2);
  xnor xnor_16 (xnor_16_out, B1, A1);
  not not_8 (not_8_out, A0);
  and and_1 (and_1_out, A3, not_1_out);
  and and_2 (and_2_out, xnor_1_out, A2, not_2_out);
  and and_3 (and_3_out, xnor_2_out, xnor_3_out, A1, not_3_out);
  and and_4 (and_4_out, xnor_4_out, xnor_5_out, xnor_6_out, A0, not_4_out);
  and and_5 (AequalsB_2, xnor_7_out, xnor_8_out, xnor_9_out, xnor_10_out, AequalsB);
  and and_6 (and_6_out, B3, not_5_out);
  and and_7 (and_7_out, xnor_11_out, B2, not_6_out);
  and and_8 (and_8_out, xnor_12_out, xnor_13_out, B1, not_7_out);
  and and_9 (and_9_out, xnor_14_out, xnor_15_out, xnor_16_out, B0, not_8_out);
  or or_1 (or_1_out, and_1_out, and_2_out, and_3_out, and_4_out);
  or or_2 (or_2_out, and_6_out, and_7_out, and_8_out, and_9_out);
  and and_10 (AgreaterthanB_2, AgreaterthanB, or_1_out);
  and and_11 (AlessthanB_2, AlessthanB, or_2_out);
endmodule

module _7segmentdisplay (
  input  AlargerthanB,
  input  AequalsB,
  input  AlessthanB,
  input  D3,
  input  D2,
  input  D1,
  input  D0,
  output Sa,
  output Sb,
  output Sc,
  output Sd,
  output Se,
  output Sf,
  output Sg
);

  wire and_1_out, and_2_out, and_3_out, and_4_out, and_5_out, and_6_out, and_7_out, and_8_out, and_9_out,
       and_10_out, and_11_out, and_12_out, and_13_out, and_14_out, and_15_out, and_16_out, and_17_out,
       and_18_out, and_19_out, and_20_out, and_21_out, and_22_out, and_23_out, and_24_out, and_25_out,
       not_1_out, not_2_out, not_3_out, not_4_out, not_5_out, not_6_out, not_7_out, not_8_out, not_9_out,
       not_10_out, not_11_out, not_12_out, not_13_out, not_14_out, not_15_out, not_16_out, not_17_out,
       not_18_out, not_19_out, not_20_out, not_21_out, not_22_out, not_23_out, not_24_out, not_25_out,
       not_26_out, not_27_out, not_28_out, not_29_out, not_30_out, not_31_out, not_32_out, not_33_out,
       not_34_out, not_35_out, not_36_out, not_37_out, not_38_out, not_39_out, not_40_out, not_41_out,
       not_42_out, not_43_out, not_44_out, not_45_out, not_46_out, not_47_out, not_48_out, not_49_out,
       not_50_out, or_1_out, or_2_out;

  or or_1 (or_1_out, AlargerthanB, AequalsB, AlessthanB);
  or or_2 (or_2_out, AlargerthanB, AequalsB, AlessthanB);
  not not_1 (not_1_out, D3);
  not not_2 (not_2_out, D3);
  not not_3 (not_3_out, D2);
  not not_4 (not_4_out, D0);
  not not_5 (not_5_out, D3);
  not not_6 (not_6_out, D2);
  not not_7 (not_7_out, D1);
  not not_8 (not_8_out, D3);
  not not_9 (not_9_out, D2);
  not not_10 (not_10_out, D2);
  not not_11 (not_11_out, D1);
  not not_12 (not_12_out, D3);
  not not_13 (not_13_out, D1);
  not not_14 (not_14_out, D0);
  not not_15 (not_15_out, D3);
  not not_16 (not_16_out, D2);
  not not_17 (not_17_out, D1);
  not not_18 (not_18_out, D3);
  not not_19 (not_19_out, D3);
  not not_20 (not_20_out, D2);
  not not_21 (not_21_out, D1);
  not not_22 (not_22_out, D0);
  not not_23 (not_23_out, D3);
  not not_24 (not_24_out, D2);
  not not_25 (not_25_out, D3);
  not not_26 (not_26_out, D0);
  not not_27 (not_27_out, D3);
  not not_28 (not_28_out, D1);
  not not_29 (not_29_out, D2);
  not not_30 (not_30_out, D1);
  not not_31 (not_31_out, D0);
  not not_32 (not_32_out, D3);
  not not_33 (not_33_out, D0);
  not not_34 (not_34_out, D3);
  not not_35 (not_35_out, D1);
  not not_36 (not_36_out, D0);
  not not_37 (not_37_out, D3);
  not not_38 (not_38_out, D1);
  not not_39 (not_39_out, D3);
  not not_40 (not_40_out, D0);
  not not_41 (not_41_out, D2);
  not not_42 (not_42_out, D1);
  not not_43 (not_43_out, D3);
  not not_44 (not_44_out, D2);
  not not_45 (not_45_out, D3);
  not not_46 (not_46_out, D0);
  not not_47 (not_47_out, D3);
  not not_48 (not_48_out, D1);
  not not_49 (not_49_out, D2);
  not not_50 (not_50_out, D1);
  and and_1 (and_1_out, not_1_out, D1);
  and and_2 (and_2_out, not_2_out, not_3_out, not_4_out);
  and and_3 (and_3_out, not_5_out, D2, D0);
  and and_4 (and_4_out, D3, not_6_out, not_7_out);
  and and_5 (and_5_out, not_8_out, not_9_out);
  and and_6 (and_6_out, not_10_out, not_11_out);
  and and_7 (and_7_out, not_12_out, not_13_out, not_14_out);
  and and_8 (and_8_out, not_15_out, D1, D0);
  and and_9 (and_9_out, not_16_out, not_17_out);
  and and_10 (and_10_out, not_18_out, D0);
  and and_11 (and_11_out, not_19_out, D2);
  and and_12 (and_12_out, not_20_out, not_21_out, not_22_out);
  and and_13 (and_13_out, not_23_out, not_24_out, D1);
  and and_14 (and_14_out, not_25_out, D1, not_26_out);
  and and_15 (and_15_out, not_27_out, D2, not_28_out, D0);
  and and_16 (and_16_out, not_29_out, not_30_out, not_31_out);
  and and_17 (and_17_out, not_32_out, D1, not_33_out);
  and and_18 (and_18_out, not_34_out, not_35_out, not_36_out);
  and and_19 (and_19_out, not_37_out, D2, not_38_out);
  and and_20 (and_20_out, not_39_out, D2, not_40_out);
  and and_21 (and_21_out, D3, not_41_out, not_42_out);
  and and_22 (and_22_out, not_43_out, not_44_out, D1);
  and and_23 (and_23_out, not_45_out, D1, not_46_out);
  and and_24 (and_24_out, not_47_out, D2, not_48_out);
  and and_25 (and_25_out, D3, not_49_out, not_50_out);
  or or_3 (Sa, and_1_out, and_2_out, and_3_out, and_4_out);
  or or_4 (Sb, and_5_out, and_6_out, or_1_out, and_7_out, and_8_out);
  or or_5 (Sc, and_9_out, and_10_out, or_2_out, and_11_out);
  or or_6 (Sd, and_12_out, and_13_out, and_14_out, and_15_out);
  or or_7 (Se, and_16_out, and_17_out);
  or or_8 (Sf, and_18_out, and_19_out, and_20_out, and_21_out);
  or or_9 (Sg, and_22_out, and_23_out, and_24_out, and_25_out);
endmodule

module _7segmentdisplay_comparison (
  input  AlargerthanB,
  input  AequalsB,
  input  AlessthanB,
  output Sb,
  output Sc
);

  or or_1 (Sb, AlargerthanB, AequalsB, AlessthanB);
  or or_2 (Sc, AlargerthanB, AequalsB, AlessthanB);
endmodule

module Comparison (
  input  AgreaterthanB,
  input  AequalsB,
  input  AlessthanB,
  input  [3:0] A,
  input  [3:0] B,
  output A___B,
  output A___B_2,
  output A___B_3
);

  wire comparator_1_eq, comparator_1_gt, comparator_1_lt;

  Comparator #(.width(4)) comparator_1 (.a(A), .b(B), .gt(comparator_1_gt), .eq(comparator_1_eq), .lt(comparator_1_lt));
  assign A___B = AequalsB ? comparator_1_eq : 1'bz;  // Controlled_Buffer controlled_buffer_1
  assign A___B_2 = AgreaterthanB ? comparator_1_gt : 1'bz;  // Controlled_Buffer controlled_buffer_2
  assign A___B_3 = AlessthanB ? comparator_1_lt : 1'bz;  // Controlled_Buffer controlled_buffer_3
endmodule

module Logic (
  input  [3:0] in_1,
  input  [3:0] in_2,
  input  AandB,
  input  AorB,
  input  AxorB,
  input  AnxorB
);

  wire [3:0] and_1_out, controlled_buffer_1_out, controlled_buffer_2_out, controlled_buffer_3_out,
       controlled_buffer_4_out, or_1_out, xnor_1_out, xor_1_out;

  assign and_1_out = in_1 & in_2;  // AND_Gate and_1, 4 bits wide
  assign or_1_out = in_1 | in_2;  // OR_Gate or_1, 4 bits wide
  assign xor_1_out = in_1 ^ in_2;  // XOR_Gate xor_1, 4 bits wide
  assign xnor_1_out = ~(in_1 ^ in_2);  // XNOR_Gate xnor_1, 4 bits wide
  assign controlled_buffer_1_out = AandB ? and_1_out : 4'bz;  // Controlled_Buffer controlled_buffer_1
  assign controlled_buffer_2_out = AorB ? or_1_out : 4'bz;  // Controlled_Buffer controlled_buffer_2
  assign controlled_buffer_3_out = AxorB ? xor_1_out : 4'bz;  // Controlled_Buffer controlled_buffer_3
  assign controlled_buffer_4_out = AnxorB ? xnor_1_out : 4'bz;  // Controlled_Buffer controlled_buffer_4
endmodule
