// Logisim project Exercise2.circ as structural Verilog: 1 circuit, main circuit main
module main (
);

  wire button_1_out, button_2_out, lab1testhelper_1_p3, lab1testhelper_1_p4, lab1testhelper_1_p5, nand_1_out,
       nor_1_out, not_1_out, not_2_out, or_1_out, xnor_1_out;

  Button button_1 (.out(button_1_out));
  Button button_2 (.out(button_2_out));
  // Lab1TestHelper lab1testhelper_1: pin names not known; wires that end beside it: button_1_out, button_2_out, lab1testhelper_1_p3, lab1testhelper_1_p4, lab1testhelper_1_p5
  LED B (.in(lab1testhelper_1_p4));
  LED C (.in(lab1testhelper_1_p5));
  LED A (.in(lab1testhelper_1_p3));
  nor nor_1 (nor_1_out, lab1testhelper_1_p3, lab1testhelper_1_p5);
  nand nand_1 (nand_1_out, lab1testhelper_1_p3, lab1testhelper_1_p4);
  not not_1 (not_1_out, lab1testhelper_1_p4);
  or or_1 (or_1_out, nand_1_out, not_1_out);
  not not_2 (not_2_out, or_1_out);
  NotExactlyOne xnor_1 (.out(xnor_1_out), .in0(not_2_out), .in1(lab1testhelper_1_p4), .in2(nor_1_out));
  LED X (.in(xnor_1_out));

  // Notes on the sheet:
  //   A
  //   B
  //   C
  //   X
endmodule
