// Logisim project Exercise3.circ as structural Verilog: 1 circuit, main circuit main
module main (
);

  wire and_1_out, and_2_out, and_3_out, and_4_out, and_5_out, button_1_out, button_2_out,
       lab1testhelper_1_p3, lab1testhelper_1_p4, lab1testhelper_1_p5, not_1_out, not_2_out, not_3_out,
       not_4_out, not_5_out, not_6_out, not_7_out, not_8_out, or_1_out, or_2_out, or_3_out, or_4_out;

  Button button_1 (.out(button_1_out));
  Button button_2 (.out(button_2_out));
  LED led_1 (.in(lab1testhelper_1_p3));
  // Lab1TestHelper lab1testhelper_1: pin names not known; wires that end beside it: button_1_out, button_2_out, lab1testhelper_1_p3, lab1testhelper_1_p4, lab1testhelper_1_p5
  LED led_2 (.in(lab1testhelper_1_p5));
  LED led_3 (.in(lab1testhelper_1_p4));
  or or_1 (or_1_out, lab1testhelper_1_p3, lab1testhelper_1_p5);
  not not_1 (not_1_out, and_1_out);
  and and_1 (and_1_out, lab1testhelper_1_p3, lab1testhelper_1_p4);
  not not_2 (not_2_out, lab1testhelper_1_p4);
  not not_3 (not_3_out, or_1_out);
  or or_2 (or_2_out, not_1_out, not_2_out);
  not not_4 (not_4_out, or_2_out);
  not not_5 (not_5_out, not_4_out);
  not not_6 (not_6_out, lab1testhelper_1_p4);
  not not_7 (not_7_out, not_3_out);
  and and_2 (and_2_out, not_4_out, lab1testhelper_1_p4, not_3_out);
  and and_3 (and_3_out, not_4_out, not_6_out, not_7_out);
  and and_4 (and_4_out, not_5_out, lab1testhelper_1_p4, not_7_out);
  and and_5 (and_5_out, not_5_out, not_6_out, not_3_out);
  or or_3 (or_3_out, and_3_out, and_4_out, and_5_out);
  not not_8 (not_8_out, or_3_out);
  or or_4 (or_4_out, and_2_out, not_8_out);
  LED X (.in(or_4_out));

  // Notes on the sheet:
  //   A
  //   B
  //   C
  //   X
endmodule
