// Logisim project ex2.circ as structural Verilog
module ex2 (
  input  D3,
  input  D2,
  input  D1,
  input  D0,
  output Sa,
  output Sb,
  output Sc,
  output Sd,
  output Se,
  output Sf,
  output Sg
);

  wire and_1_out, and_2_out, and_3_out, and_4_out, and_5_out, and_6_out, and_7_out, and_8_out, and_9_out,
       and_10_out, and_11_out, and_12_out, and_13_out, and_14_out, and_15_out, and_16_out, and_17_out,
       and_18_out, and_19_out, and_20_out, and_21_out, and_22_out, and_23_out, and_24_out, and_25_out,
       not_1_out, not_2_out, not_3_out, not_4_out, not_5_out, not_6_out, not_7_out, not_8_out, not_9_out,
       not_10_out, not_11_out, not_12_out, not_13_out, not_14_out, not_15_out, not_16_out, not_17_out,
       not_18_out, not_19_out, not_20_out, not_21_out, not_22_out, not_23_out, not_24_out, not_25_out,
       not_26_out, not_27_out, not_28_out, not_29_out, not_30_out, not_31_out, not_32_out, not_33_out,
       not_34_out, not_35_out, not_36_out, not_37_out, not_38_out, not_39_out, not_40_out, not_41_out,
       not_42_out, not_43_out, not_44_out, not_45_out, not_46_out, not_47_out, not_48_out, not_49_out,
       not_50_out;

  not not_1 (not_1_out, D3);
  and and_1 (and_1_out, not_1_out, D1);
  not not_2 (not_2_out, D3);
  and and_2 (and_2_out, not_2_out, not_3_out, not_4_out);
  not not_3 (not_3_out, D2);
  not not_4 (not_4_out, D0);
  not not_5 (not_5_out, D3);
  and and_3 (and_3_out, not_5_out, D2, D0);
  not not_6 (not_6_out, D2);
  and and_4 (and_4_out, D3, not_6_out, not_7_out);
  not not_7 (not_7_out, D1);
  not not_8 (not_8_out, D3);
  and and_5 (and_5_out, not_8_out, not_9_out);
  not not_9 (not_9_out, D2);
  not not_10 (not_10_out, D2);
  and and_6 (and_6_out, not_10_out, not_11_out);
  not not_11 (not_11_out, D1);
  not not_12 (not_12_out, D3);
  and and_7 (and_7_out, not_12_out, not_13_out, not_14_out);
  not not_13 (not_13_out, D1);
  not not_14 (not_14_out, D0);
  not not_15 (not_15_out, D3);
  and and_8 (and_8_out, not_15_out, D1, D0);
  not not_16 (not_16_out, D2);
  and and_9 (and_9_out, not_16_out, not_17_out);
  not not_17 (not_17_out, D1);
  not not_18 (not_18_out, D3);
  and and_10 (and_10_out, not_18_out, D0);
  not not_19 (not_19_out, D3);
  and and_11 (and_11_out, not_19_out, D2);
  not not_20 (not_20_out, D2);
  not not_21 (not_21_out, D1);
  not not_22 (not_22_out, D0);
  not not_23 (not_23_out, D3);
  not not_24 (not_24_out, D2);
  not not_25 (not_25_out, D3);
  not not_26 (not_26_out, D0);
  not not_27 (not_27_out, D3);
  not not_28 (not_28_out, D1);
  not not_29 (not_29_out, D2);
  and and_12 (and_12_out, not_29_out, not_30_out, not_31_out);
  not not_30 (not_30_out, D1);
  not not_31 (not_31_out, D0);
  not not_32 (not_32_out, D3);
  and and_13 (and_13_out, not_32_out, D1, not_33_out);
  not not_33 (not_33_out, D0);
  not not_34 (not_34_out, D3);
  and and_14 (and_14_out, not_34_out, not_35_out, not_36_out);
  not not_35 (not_35_out, D1);
  not not_36 (not_36_out, D0);
  not not_37 (not_37_out, D3);
  and and_15 (and_15_out, not_37_out, D2, not_38_out);
  not not_38 (not_38_out, D1);
  not not_39 (not_39_out, D3);
  and and_16 (and_16_out, not_39_out, D2, not_40_out);
  not not_40 (not_40_out, D0);
  not not_41 (not_41_out, D2);
  and and_17 (and_17_out, D3, not_41_out, not_42_out);
  not not_42 (not_42_out, D1);
  not not_43 (not_43_out, D3);
  and and_18 (and_18_out, not_43_out, not_44_out, D1);
  not not_44 (not_44_out, D2);
  not not_45 (not_45_out, D3);
  and and_19 (and_19_out, not_45_out, D1, not_46_out);
  not not_46 (not_46_out, D0);
  not not_47 (not_47_out, D3);
  and and_20 (and_20_out, not_47_out, D2, not_48_out);
  not not_48 (not_48_out, D1);
  and and_21 (and_21_out, D3, not_49_out, not_50_out);
  not not_49 (not_49_out, D2);
  not not_50 (not_50_out, D1);
  or or_1 (Sa, and_1_out, and_2_out, and_3_out, and_4_out);
  or or_2 (Sb, and_5_out, and_6_out, and_7_out, and_8_out);
  or or_3 (Sc, and_9_out, and_10_out, and_11_out);
  and and_22 (and_22_out, not_20_out, not_21_out, not_22_out);
  and and_23 (and_23_out, not_23_out, not_24_out, D1);
  and and_24 (and_24_out, not_25_out, D1, not_26_out);
  and and_25 (and_25_out, not_27_out, D2, not_28_out, D0);
  or or_4 (Se, and_12_out, and_13_out);
  or or_5 (Sf, and_14_out, and_15_out, and_16_out, and_17_out);
  or or_6 (Sg, and_18_out, and_19_out, and_20_out, and_21_out);
  or or_7 (Sd, and_22_out, and_23_out, and_24_out, and_25_out);
  _7_Segment_Display u_7_segment_display_1 (.g(Sg), .f(Sf), .a(Sa), .b(Sb), .e(Se), .d(Sd), .c(Sc));  // open: dp
endmodule

module ex_2inputgates (
  input  D3,
  input  D2,
  input  D1,
  input  D0,
  output Sa,
  output Sb,
  output Sc,
  output Sd,
  output Se,
  output Sf,
  output Sg
);

  wire and_1_out, and_2_out, and_3_out, and_4_out, and_5_out, and_6_out, and_7_out, and_8_out, and_9_out,
       and_10_out, and_11_out, and_12_out, and_13_out, and_14_out, and_15_out, and_16_out, and_17_out,
       and_18_out, and_19_out, and_20_out, and_21_out, and_22_out, and_23_out, and_24_out, and_25_out,
       and_26_out, and_27_out, and_28_out, and_29_out, and_30_out, and_31_out, and_32_out, and_33_out,
       and_34_out, and_35_out, and_36_out, and_37_out, and_38_out, and_39_out, and_40_out, and_41_out,
       and_42_out, and_43_out, and_44_out, and_45_out, not_1_out, not_2_out, not_3_out, not_4_out, not_5_out,
       not_6_out, not_7_out, not_8_out, not_9_out, not_10_out, not_11_out, not_12_out, not_13_out,
       not_14_out, not_15_out, not_16_out, not_17_out, not_18_out, not_19_out, not_20_out, not_21_out,
       not_22_out, not_23_out, not_24_out, not_25_out, not_26_out, not_27_out, not_28_out, not_29_out,
       not_30_out, not_31_out, not_32_out, not_33_out, not_34_out, not_35_out, not_36_out, not_37_out,
       not_38_out, not_39_out, not_40_out, not_41_out, not_42_out, not_43_out, not_44_out, not_45_out,
       not_46_out, not_47_out, not_48_out, not_49_out, not_50_out, or_1_out, or_2_out, or_3_out, or_4_out,
       or_5_out, or_7_out, or_8_out, or_10_out, or_11_out, or_12_out, or_13_out;

  not not_1 (not_1_out, D3);
  and and_1 (and_1_out, not_1_out, not_2_out);
  not not_2 (not_2_out, D2);
  not not_3 (not_3_out, D0);
  not not_4 (not_4_out, D3);
  not not_5 (not_5_out, D3);
  and and_2 (and_2_out, not_5_out, D2);
  and and_3 (and_3_out, D3, not_6_out);
  not not_6 (not_6_out, D2);
  not not_7 (not_7_out, D1);
  not not_8 (not_8_out, D3);
  not not_9 (not_9_out, D2);
  not not_10 (not_10_out, D3);
  and and_4 (and_4_out, not_10_out, not_11_out);
  not not_11 (not_11_out, D1);
  not not_12 (not_12_out, D0);
  not not_13 (not_13_out, D2);
  not not_14 (not_14_out, D1);
  not not_15 (not_15_out, D3);
  and and_5 (and_5_out, not_15_out, D1);
  not not_16 (not_16_out, D2);
  and and_6 (and_6_out, not_16_out, not_17_out);
  not not_17 (not_17_out, D1);
  not not_18 (not_18_out, D3);
  and and_7 (and_7_out, not_18_out, D0);
  not not_19 (not_19_out, D3);
  not not_20 (not_20_out, D2);
  and and_8 (and_8_out, not_20_out, not_21_out);
  not not_21 (not_21_out, D1);
  not not_22 (not_22_out, D0);
  not not_23 (not_23_out, D3);
  and and_9 (and_9_out, not_23_out, not_24_out);
  not not_24 (not_24_out, D2);
  not not_25 (not_25_out, D3);
  and and_10 (and_10_out, not_25_out, D1);
  not not_26 (not_26_out, D0);
  not not_27 (not_27_out, D3);
  and and_11 (and_11_out, not_27_out, D2);
  not not_28 (not_28_out, D1);
  and and_12 (and_12_out, not_28_out, D0);
  not not_29 (not_29_out, D2);
  and and_13 (and_13_out, not_29_out, not_30_out);
  not not_30 (not_30_out, D1);
  not not_31 (not_31_out, D0);
  not not_32 (not_32_out, D3);
  and and_14 (and_14_out, not_32_out, D1);
  not not_33 (not_33_out, D0);
  not not_34 (not_34_out, D3);
  and and_15 (and_15_out, not_34_out, not_35_out);
  not not_35 (not_35_out, D1);
  not not_36 (not_36_out, D0);
  not not_37 (not_37_out, D3);
  and and_16 (and_16_out, not_37_out, D2);
  not not_38 (not_38_out, D1);
  not not_39 (not_39_out, D3);
  and and_17 (and_17_out, not_39_out, D2);
  not not_40 (not_40_out, D0);
  and and_18 (and_18_out, D3, not_41_out);
  not not_41 (not_41_out, D2);
  not not_42 (not_42_out, D1);
  not not_43 (not_43_out, D3);
  and and_19 (and_19_out, not_43_out, not_44_out);
  not not_44 (not_44_out, D2);
  not not_45 (not_45_out, D3);
  and and_20 (and_20_out, not_45_out, D2);
  not not_46 (not_46_out, D1);
  not not_47 (not_47_out, D3);
  and and_21 (and_21_out, not_47_out, D2);
  not not_48 (not_48_out, D0);
  and and_22 (and_22_out, D3, not_49_out);
  not not_49 (not_49_out, D2);
  not not_50 (not_50_out, D1);
  and and_23 (and_23_out, and_1_out, not_3_out);
  and and_24 (and_24_out, not_4_out, D1);
  and and_25 (and_25_out, and_2_out, D0);
  and and_26 (and_26_out, and_3_out, not_7_out);
  and and_27 (and_27_out, not_8_out, not_9_out);
  and and_28 (and_28_out, and_4_out, not_12_out);
  and and_29 (and_29_out, not_13_out, not_14_out);
  and and_30 (and_30_out, and_5_out, D0);
  or or_1 (or_1_out, and_6_out, and_7_out);
  and and_31 (and_31_out, not_19_out, D2);
  and and_32 (and_32_out, and_8_out, not_22_out);
  and and_33 (and_33_out, and_9_out, D1);
  and and_34 (and_34_out, and_10_out, not_26_out);
  and and_35 (and_35_out, and_11_out, and_12_out);
  and and_36 (and_36_out, and_13_out, not_31_out);
  and and_37 (and_37_out, and_14_out, not_33_out);
  and and_38 (and_38_out, and_15_out, not_36_out);
  and and_39 (and_39_out, and_16_out, not_38_out);
  and and_40 (and_40_out, and_17_out, not_40_out);
  and and_41 (and_41_out, and_18_out, not_42_out);
  and and_42 (and_42_out, and_19_out, D1);
  and and_43 (and_43_out, and_20_out, not_46_out);
  and and_44 (and_44_out, and_21_out, not_48_out);
  and and_45 (and_45_out, and_22_out, not_50_out);
  or or_2 (or_2_out, and_23_out, and_24_out);
  or or_3 (or_3_out, and_25_out, and_26_out);
  or or_4 (or_4_out, and_27_out, and_28_out);
  or or_5 (or_5_out, and_29_out, and_30_out);
  or or_6 (Sc, or_1_out, and_31_out);
  or or_7 (or_7_out, and_32_out, and_33_out);
  or or_8 (or_8_out, and_34_out, and_35_out);
  or or_9 (Se, and_36_out, and_37_out);
  or or_10 (or_10_out, and_38_out, and_39_out);
  or or_11 (or_11_out, and_40_out, and_41_out);
  or or_12 (or_12_out, and_42_out, and_43_out);
  or or_13 (or_13_out, and_44_out, and_45_out);
  or or_14 (Sa, or_2_out, or_3_out);
  or or_15 (Sb, or_4_out, or_5_out);
  or or_16 (Sd, or_7_out, or_8_out);
  or or_17 (Sf, or_10_out, or_11_out);
  or or_18 (Sg, or_12_out, or_13_out);
  _7_Segment_Display u_7_segment_display_1 (.g(Sg), .f(Sf), .a(Sa), .b(Sb), .e(Se), .d(Sd), .c(Sc));  // open: dp
endmodule
