// Logisim project Exercise1_1.circ as structural Verilog: 1 circuit, main circuit 1bitfulladder
module _1bitfulladder (
  input  Cin,
  input  Ai,
  input  Bi,
  output Si,
  output Cout
);

  wire and_1_out, and_2_out, and_3_out, and_4_out, and_5_out, and_6_out, and_7_out, not_1_out, not_2_out,
       not_3_out, not_4_out, not_5_out, not_6_out;

  not not_1 (not_1_out, Cin);
  not not_2 (not_2_out, Ai);
  not not_3 (not_3_out, Cin);
  not not_4 (not_4_out, Bi);
  not not_5 (not_5_out, Ai);
  not not_6 (not_6_out, Bi);
  and and_1 (and_1_out, Ai, Bi);
  and and_2 (and_2_out, Cin, Bi);
  and and_3 (and_3_out, Cin, Ai);
  and and_4 (and_4_out, not_1_out, not_2_out, Bi);
  and and_5 (and_5_out, not_3_out, Ai, not_4_out);
  and and_6 (and_6_out, Cin, not_5_out, not_6_out);
  and and_7 (and_7_out, Cin, Ai, Bi);
  or or_1 (Cout, and_1_out, and_2_out, and_3_out);
  or or_2 (Si, and_4_out, and_5_out, and_6_out, and_7_out);
endmodule
