// Logisim project Exercise1_4.circ as structural Verilog: 4 circuits, main circuit 1bitfulladder
module _1bitfulladder (
  input  Cin,
  input  Ai,
  input  Bi,
  output Si,
  output Cout
);

  wire and_1_out, and_2_out, and_3_out, and_4_out, and_5_out, and_6_out, and_7_out, not_1_out, not_2_out,
       not_3_out, not_4_out, not_5_out, not_6_out;

  not not_1 (not_1_out, Cin);
  not not_2 (not_2_out, Ai);
  not not_3 (not_3_out, Cin);
  not not_4 (not_4_out, Bi);
  not not_5 (not_5_out, Ai);
  not not_6 (not_6_out, Bi);
  and and_1 (and_1_out, Ai, Bi);
  and and_2 (and_2_out, Cin, Bi);
  and and_3 (and_3_out, Cin, Ai);
  and and_4 (and_4_out, not_1_out, not_2_out, Bi);
  and and_5 (and_5_out, not_3_out, Ai, not_4_out);
  and and_6 (and_6_out, Cin, not_5_out, not_6_out);
  and and_7 (and_7_out, Cin, Ai, Bi);
  or or_1 (Cout, and_1_out, and_2_out, and_3_out);
  or or_2 (Si, and_4_out, and_5_out, and_6_out, and_7_out);
endmodule

module _4bitadder (
  input  B3,
  input  B2,
  input  B1,
  input  B0,
  input  A3,
  input  A2,
  input  A1,
  input  A0,
  output C0,
  output Cout,
  output S3,
  output S2,
  output S1,
  output S0
);

  wire n1bitfulladder_2_cout, n1bitfulladder_3_cout, n1bitfulladder_4_cout;

  _1bitfulladder u_1bitfulladder_1 (.Cin(n1bitfulladder_2_cout), .Ai(A3), .Bi(B3), .Si(S3), .Cout(Cout));
  _1bitfulladder u_1bitfulladder_2 (
    .Cin(n1bitfulladder_3_cout), .Ai(A2), .Bi(B2), .Si(S2), .Cout(n1bitfulladder_2_cout));
  _1bitfulladder u_1bitfulladder_3 (
    .Cin(n1bitfulladder_4_cout), .Ai(A1), .Bi(B1), .Si(S1), .Cout(n1bitfulladder_3_cout));
  _1bitfulladder u_1bitfulladder_4 (.Cin(1'b0), .Ai(A0), .Bi(B0), .Si(S0), .Cout(n1bitfulladder_4_cout));

  assign C0 = 1'b0;
endmodule

module _4bitsubtractor (
  input  B3,
  input  B2,
  input  B1,
  input  B0,
  input  A3,
  input  A2,
  input  A1,
  input  A0,
  output C0,
  output Cout,
  output S3,
  output S2,
  output S1,
  output S0,
  output Overflow
);

  wire n1bitfulladder_2_cout, n1bitfulladder_3_cout, n1bitfulladder_4_cout, not_1_out, not_2_out, not_3_out,
       not_4_out;

  not not_1 (not_1_out, B3);
  _1bitfulladder u_1bitfulladder_1 (.Cin(n1bitfulladder_2_cout), .Ai(A3), .Bi(not_1_out), .Si(S3), .Cout(Cout));
  xor xor_1 (Overflow, n1bitfulladder_2_cout, Cout);
  not not_2 (not_2_out, B2);
  _1bitfulladder u_1bitfulladder_2 (
    .Cin(n1bitfulladder_3_cout), .Ai(A2), .Bi(not_2_out), .Si(S2), .Cout(n1bitfulladder_2_cout));
  not not_3 (not_3_out, B1);
  _1bitfulladder u_1bitfulladder_3 (
    .Cin(n1bitfulladder_4_cout), .Ai(A1), .Bi(not_3_out), .Si(S1), .Cout(n1bitfulladder_3_cout));
  not not_4 (not_4_out, B0);
  _1bitfulladder u_1bitfulladder_4 (.Cin(1'b1), .Ai(A0), .Bi(not_4_out), .Si(S0), .Cout(n1bitfulladder_4_cout));

  assign C0 = 1'b1;
endmodule

module _4bitaddersubtractor (
  input  Mode,
  input  B3,
  input  B2,
  input  B1,
  input  B0,
  input  A3,
  input  A2,
  input  A1,
  input  A0,
  output C0,
  output Cout,
  output S3,
  output S2,
  output S1,
  output S0,
  output Overflow
);

  wire n1bitfulladder_2_cout, n1bitfulladder_3_cout, n1bitfulladder_4_cout, xor_1_out, xor_3_out, xor_4_out,
       xor_5_out;

  xor xor_1 (xor_1_out, Mode, B3);
  _1bitfulladder u_1bitfulladder_1 (.Cin(n1bitfulladder_2_cout), .Ai(A3), .Bi(xor_1_out), .Si(S3), .Cout(Cout));
  xor xor_2 (Overflow, n1bitfulladder_2_cout, Cout);
  xor xor_3 (xor_3_out, Mode, B2);
  _1bitfulladder u_1bitfulladder_2 (
    .Cin(n1bitfulladder_3_cout), .Ai(A2), .Bi(xor_3_out), .Si(S2), .Cout(n1bitfulladder_2_cout));
  xor xor_4 (xor_4_out, Mode, B1);
  _1bitfulladder u_1bitfulladder_3 (
    .Cin(n1bitfulladder_4_cout), .Ai(A1), .Bi(xor_4_out), .Si(S1), .Cout(n1bitfulladder_3_cout));
  xor xor_5 (xor_5_out, Mode, B0);
  _1bitfulladder u_1bitfulladder_4 (.Cin(Mode), .Ai(A0), .Bi(xor_5_out), .Si(S0), .Cout(n1bitfulladder_4_cout));

  assign C0 = Mode;
endmodule
